# Fritzing sketch ReTouch_UNO-ADXL362 (saved by Fritzing 0.8.7b)
breadboards: 1

parts:
  ReTouch = Arduino Uno (Rev3)
  ADXL362 = Tri-Axis Accelerometer Breakout - ADXL362
  Copper_foil_2 = CAPSENSE_PAD [package=capsense_pad]
  Copper_foil = CAPSENSE_PAD [package=capsense_pad]
  Copper_foil_3 = CAPSENSE_PAD [package=capsense_pad]
  R1 = Resistor [tolerance=±5% resistance=100k package=THT]
  R2 = Resistor [tolerance=±5% resistance=100k package=THT]
  R3 = Resistor [tolerance=±5% resistance=100k package=THT]
  LED1 = LED - 5mm [color="Green (560nm)" package="5 mm [THT]"]
  R4 = Resistor [tolerance=±5% resistance=220 package=THT]

nets:
  N1: ReTouch.D8, Copper_foil_3.RECEIVE, R3.Pin_1
  N2: ReTouch.D9_PWM, LED1.anode
  N3: ReTouch.D10_PWM/SS, ADXL362.MOSI
  N4: ReTouch.D11_PWM/MOSI, ADXL362.MISO
  N5: ReTouch.D12/MISO, ADXL362.CS
  N6: ReTouch.D13/SCK, ADXL362.SCK
  N7: ReTouch.D2, ADXL362.INT1
  N8: ReTouch.D3_PWM, R1.Pin_0
  N9: ReTouch.D4, Copper_foil.RECEIVE, R1.Pin_1
  N10: ReTouch.D5_PWM, R2.Pin_0
  N11: ReTouch.D6_PWM, Copper_foil_2.RECEIVE, R2.Pin_1
  N12: ReTouch.D7, R3.Pin_0
  3V3: ReTouch.3V3, ADXL362.VCC
  N13: ADXL362.GND, R4.Pin_0
  N14: LED1.cathode, R4.Pin_1

custom parts:
  Tri-Axis Accelerometer Breakout - ADXL362: Description: Low-power three-axis angular rate sensor.
  CAPSENSE_PAD: Generic copper pad for a capacitive touch sensor.
